# Fritzing sketch flipdot_by_hbridge (saved by Fritzing 0.9.0b)
breadboards: 1

parts:
  Bauteil1 = Arduino Uno (Rev3)
  part = DC Motor  # not connected
  IC1 = L293D [package=THT]
  VCC1 = Battery block 9V  # not connected

nets:
  N1: Bauteil1.D10_PWM/SS, IC1.In_4
  N2: Bauteil1.D11_PWM/MOSI, IC1.In_3
  N3: Bauteil1.GND, IC1.0V
  N4: Bauteil1.5V, IC1.+V
  N5: Bauteil1.VIN, IC1.+Vmotor
